# Fritzing sketch Elektrische schema (saved by Fritzing 0.9.10b)

parts:
  Onderdeel2 = Arduino Uno (Rev3)
  Onderdeel3 = Thermal Printer
  VCC1 = 4 x AAA Battery Mount  # not connected

nets:
  N1: Onderdeel2.D5_PWM, Onderdeel3.RXD
  N2: Onderdeel2.D6_PWM, Onderdeel3.TXD
  GND: Onderdeel2.GND, Onderdeel3.GND
